// Logisim project CIRCUITO.circ as structural Verilog: 1 circuit, main circuit main
module main (
  input  A3,
  input  A2,
  input  A1,
  input  C,
  output R3,
  output R2,
  output R1
);

  wire adder_1_out, adder_2_cout, adder_2_out, adder_3_cout, adder_3_out, adder_4_out, adder_5_cout,
       adder_5_out, adder_6_cout, adder_6_out, and_1_out, and_2_out, and_3_out, and_4_out, and_5_out,
       and_6_out, not_1_out, not_2_out, not_3_out, not_4_out, not_5_out, not_6_out, not_7_out, not_8_out,
       not_9_out, or_1_out, or_2_out, or_3_out;

  not not_1 (not_1_out, A3);
  not not_2 (not_2_out, A2);
  Adder #(.width(1)) adder_1 (.a(A3), .b(adder_2_cout), .out(adder_1_out));  // open: cin, cout
  Adder #(.width(1)) adder_2 (.a(A2), .b(adder_3_cout), .out(adder_2_out), .cout(adder_2_cout));  // open: cin
  Adder #(.width(1)) adder_3 (.a(A1), .b(not_3_out), .out(adder_3_out), .cout(adder_3_cout));  // open: cin
  not not_3 (not_3_out, C);
  not not_4 (not_4_out, A1);
  Adder #(.width(1)) adder_4 (.a(not_1_out), .b(adder_5_cout), .out(adder_4_out));  // open: cin, cout
  Adder #(.width(1)) adder_5 (.a(not_2_out), .b(adder_6_cout), .out(adder_5_out), .cout(adder_5_cout));  // open: cin
  Adder #(.width(1)) adder_6 (.a(not_4_out), .b(not_5_out), .out(adder_6_out), .cout(adder_6_cout));  // open: cin
  not not_5 (not_5_out, not_6_out);
  not not_6 (not_6_out, C);
  not not_7 (not_7_out, adder_4_out);
  not not_8 (not_8_out, adder_5_out);
  not not_9 (not_9_out, adder_6_out);
  and and_1 (and_1_out, adder_1_out, not_3_out);
  and and_2 (and_2_out, not_7_out, not_5_out);
  and and_3 (and_3_out, adder_2_out, not_3_out);
  and and_4 (and_4_out, not_8_out, not_5_out);
  and and_5 (and_5_out, adder_3_out, not_3_out);
  and and_6 (and_6_out, not_9_out, not_5_out);
  or or_1 (or_1_out, and_1_out, and_2_out);
  or or_2 (or_2_out, and_3_out, and_4_out);
  or or_3 (or_3_out, and_5_out, and_6_out);
  D_Flip_Flop #(.trigger("high")) d_ff_1 (.clk(1'b1), .D(or_1_out), .Q(R3));  // open: Qn, preset, reset
  D_Flip_Flop #(.trigger("high")) d_ff_2 (.clk(1'b1), .D(or_2_out), .Q(R2));  // open: Qn, preset, reset
  D_Flip_Flop #(.trigger("high")) d_ff_3 (.clk(1'b1), .D(or_3_out), .Q(R1));  // open: Qn, preset, reset
endmodule
