// Logisim project ESERCIZIO pag 51 teoria4.circ as structural Verilog: 1 circuit, main circuit main
module main (
  input  in_1,
  input  in_2,
  input  in_3,
  input  in_4,
  input  in_5,
  input  in_6,
  input  in_7,
  input  in_8,
  input  in_9,
  input  in_10,
  input  in_11,
  input  [2:0] in_12,
  input  in_13,
  input  in_14,
  input  in_15,
  output out_16,
  output out_17,
  output out_18
);

  wire and_1_out, and_2_out, and_3_out, and_4_out, nand_1_out, nand_2_out, nand_3_out, nand_4_out, not_1_out,
       not_2_out, not_3_out, not_4_out, not_5_out, not_6_out;

  not not_1 (not_1_out, in_1);
  not not_2 (not_2_out, in_2);
  not not_3 (not_3_out, in_3);
  not not_4 (not_4_out, in_13);
  not not_5 (not_5_out, in_14);
  not not_6 (not_6_out, in_15);
  and and_1 (and_1_out, not_1_out, not_2_out, not_3_out);
  and and_2 (and_2_out, in_1, in_2, not_3_out);
  nand nand_1 (nand_1_out, not_4_out, not_5_out, not_6_out);
  and and_3 (and_3_out, in_1, not_2_out, in_3);
  and and_4 (and_4_out, not_1_out, in_2, in_3);
  nand nand_2 (nand_2_out, not_4_out, in_14, in_15);
  nand nand_3 (nand_3_out, in_13, not_5_out, in_15);
  or or_1 (out_16, and_1_out, and_2_out, and_3_out, and_4_out);
  nand nand_4 (nand_4_out, in_13, in_14, not_6_out);
  nand nand_5 (out_18, nand_1_out, nand_2_out, nand_3_out, nand_4_out);
  Multiplexer #(.select(3)) multiplexer_1 (
    .in0(in_4), .in1(in_5), .in2(in_6), .in3(in_7), .in4(in_8), .in5(in_9), .in6(in_10), .in7(in_11),
    .out(out_17), .sel(in_12));  // open: en

  // Notes on the sheet:
  //   in_4: pull=up
  //   Teoria4 pag 51 soluzione co tutti nand
  //   Teoria4 pag 51 soluzione 1
endmodule
