// Logisim project CE_Esercizio_1_Homework_3.circ as structural Verilog: 1 circuit, main circuit main
module main (
  input  A,
  input  B,
  input  C,
  input  A_2,
  input  B_2,
  input  C_2,
  output MSB,
  output LSB,
  output out_9,
  output out_10
);

  wire and_1_out, and_2_out, and_3_out, and_4_out, and_5_out, and_6_out, and_7_out, and_8_out, and_9_out,
       and_10_out, and_11_out, not_1_out, not_2_out, not_3_out, not_4_out, not_5_out, not_6_out, not_7_out,
       not_8_out, or_1_out, xor_1_out, xor_2_out, xor_3_out;

  xor xor_1 (xor_1_out, B, A);
  not not_1 (not_1_out, C);
  not not_2 (not_2_out, B);
  not not_3 (not_3_out, A);
  xor xor_2 (xor_2_out, B, C);
  or or_1 (or_1_out, not_1_out, C);
  and and_1 (and_1_out, not_2_out, not_3_out);
  not not_4 (not_4_out, A);
  not not_5 (not_5_out, xor_2_out);
  and and_2 (and_2_out, xor_1_out, not_1_out);
  and and_3 (and_3_out, or_1_out, and_1_out);
  and and_4 (and_4_out, not_4_out, not_5_out);
  and and_5 (and_5_out, not_6_out, not_7_out);
  not not_6 (not_6_out, A_2);
  not not_7 (not_7_out, B_2);
  not not_8 (not_8_out, C_2);
  and and_6 (and_6_out, A, xor_2_out);
  or or_2 (MSB, and_2_out, and_3_out);
  or or_3 (LSB, and_4_out, and_6_out);
  or or_4 (out_10, and_5_out, and_7_out, and_8_out);
  and and_7 (and_7_out, not_7_out, not_8_out);
  and and_8 (and_8_out, not_6_out, not_8_out);
  xor xor_3 (xor_3_out, A_2, C_2);
  or or_5 (out_9, and_9_out, and_10_out, and_11_out);
  and and_9 (and_9_out, xor_3_out, B_2);
  and and_10 (and_10_out, not_6_out, not_7_out, not_8_out);
  and and_11 (and_11_out, A_2, not_7_out, C_2);

  // Notes on the sheet:
  //   !A
  //   !B
  //   !C
endmodule
