// Logisim project CE_Esercizio_2_Homework_3.circ as structural Verilog: 1 circuit, main circuit main
module main (
  input  A1,
  input  A2,
  input  A3,
  input  A4,
  input  W,
  input  S,
  input  A0,
  input  A1_2,
  input  A2_2,
  input  A3_2,
  input  W_2,
  input  S_2,
  output B1,
  output B2,
  output B3,
  output B4,
  output B0,
  output B1_2,
  output B2_2,
  output B3_2
);

  wire and_1_out, and_2_out, and_3_out, and_4_out, and_5_out, and_6_out, and_7_out, and_8_out, and_9_out,
       and_10_out, and_11_out, and_12_out, HLD_out, not_1_out, not_2_out, not_3_out, not_4_out, not_5_out,
       or_1_out, or_2_out, or_3_out, or_4_out, s1_out, s2_out, s3_out, s4_out, sh_out, SHR_out, wr_out,
       WRT_out, xor_1_out, xor_2_out, xor_3_out, xor_4_out;

  not not_1 (not_1_out, W);
  not not_2 (not_2_out, S);
  and and_1 (and_1_out, A1, wr_out);
  and and_2 (and_2_out, A2, wr_out);
  and and_3 (and_3_out, A3, wr_out);
  and and_4 (and_4_out, A4, wr_out);
  and wr (wr_out, W, not_2_out);
  and sh (sh_out, S, not_1_out);
  and and_5 (and_5_out, not_1_out, not_2_out);
  and s1 (s1_out, B4, sh_out);
  not not_3 (not_3_out, and_5_out);
  and s2 (s2_out, B1, sh_out);
  and s3 (s3_out, B2, sh_out);
  and s4 (s4_out, B3, sh_out);
  and and_6 (and_6_out, A0, WRT_out);
  and and_7 (and_7_out, A1_2, WRT_out);
  and and_8 (and_8_out, A2_2, WRT_out);
  and and_9 (and_9_out, A3_2, WRT_out);
  xor xor_1 (xor_1_out, and_1_out, s1_out);
  xor xor_2 (xor_2_out, and_2_out, s2_out);
  xor xor_3 (xor_3_out, and_3_out, s3_out);
  xor xor_4 (xor_4_out, and_4_out, s4_out);
  and and_10 (and_10_out, A0, SHR_out);
  and and_11 (and_11_out, A1_2, SHR_out);
  and and_12 (and_12_out, A2_2, SHR_out);
  D_Flip_Flop d_ff_1 (.D(xor_1_out), .clk(not_3_out), .Q(B1));  // open: Qn, preset, reset
  D_Flip_Flop d_ff_2 (.D(xor_2_out), .clk(not_3_out), .Q(B2));  // open: Qn, preset, reset
  D_Flip_Flop d_ff_3 (.D(xor_3_out), .clk(not_3_out), .Q(B3));  // open: Qn, preset, reset
  D_Flip_Flop d_ff_4 (.D(xor_4_out), .clk(not_3_out), .Q(B4));  // open: Qn, preset, reset
  or or_1 (or_1_out, and_7_out, and_10_out);
  or or_2 (or_2_out, and_8_out, and_11_out);
  or or_3 (or_3_out, and_9_out, and_12_out);
  not not_4 (not_4_out, W_2);
  not not_5 (not_5_out, S_2);
  or or_4 (or_4_out, WRT_out, SHR_out);
  D_Flip_Flop #(.trigger("high")) d_ff_5 (.clk(or_4_out), .D(and_6_out), .Q(B0));  // open: Qn, preset, reset
  D_Flip_Flop #(.trigger("high")) d_ff_6 (.clk(or_4_out), .D(or_1_out), .Q(B1_2));  // open: Qn, preset, reset
  D_Flip_Flop #(.trigger("high")) d_ff_7 (.clk(or_4_out), .D(or_2_out), .Q(B2_2));  // open: Qn, preset, reset
  D_Flip_Flop #(.trigger("high")) d_ff_8 (.clk(or_4_out), .D(or_3_out), .Q(B3_2));  // open: Qn, preset, reset
  and WRT (WRT_out, W_2, not_5_out);
  and SHR (SHR_out, S_2, not_4_out);
  // NoConnect on HLD_out
  and HLD (HLD_out, not_4_out, not_5_out);

  // Notes on the sheet:
  //   SHR
  //   !W
  //   !S
  //   W = 1 e S = 0
  //   W = 0 e S = 1
  //   W = 0 e S = 0
endmodule
