// Logisim project CP1CP2_4bit.circ as structural Verilog: 1 circuit, main circuit main
module main (
  input  [3:0] A,
  input  C,
  input  in_3,
  input  in_4,
  input  in_5,
  input  in_6,
  input  in_7,
  input  in_8,
  output [3:0] OUT
);

  wire adder_2_cout, adder_2_out, adder_3_cout, adder_3_out, adder_4_cout, adder_4_out, adder_5_out,
       and_1_out, and_2_out, and_3_out, and_4_out, and_5_out, and_6_out, and_7_out, and_8_out,
       decoder_1_out0, decoder_1_out1, not_3_out, not_4_out, not_5_out, not_6_out;
  wire [3:0] adder_1_out, not_1_out, not_2_out;

  assign not_1_out = ~A;  // NOT_Gate not_1, 4 bits wide
  assign not_2_out = ~A;  // NOT_Gate not_2, 4 bits wide
  not not_3 (not_3_out, in_4);
  not not_4 (not_4_out, in_5);
  not not_5 (not_5_out, in_6);
  not not_6 (not_6_out, in_7);
  Decoder decoder_1 (.out0(decoder_1_out0), .out1(decoder_1_out1), .sel(in_8));  // open: en
  and and_1 (and_1_out, in_4, decoder_1_out1);
  and and_2 (and_2_out, in_5, decoder_1_out1);
  and and_3 (and_3_out, in_6, decoder_1_out1);
  and and_4 (and_4_out, in_7, decoder_1_out1);
  Adder #(.width(4)) adder_1 (.a(not_2_out), .b(4'b0001), .out(adder_1_out), .cin(1'b0), .cout(in_3));
  and and_5 (and_5_out, decoder_1_out0, not_3_out);
  and and_6 (and_6_out, decoder_1_out0, not_4_out);
  and and_7 (and_7_out, decoder_1_out0, not_5_out);
  and and_8 (and_8_out, decoder_1_out0, not_6_out);
  Multiplexer #(.width(4)) multiplexer_1 (.in0(not_1_out), .in1(adder_1_out), .out(OUT), .sel(C));
  Adder #(.width(1)) adder_2 (.a(decoder_1_out1), .b(and_1_out), .out(adder_2_out), .cout(adder_2_cout));  // open: cin
  Adder #(.width(1)) adder_3 (.a(adder_2_cout), .b(and_2_out), .out(adder_3_out), .cout(adder_3_cout));  // open: cin
  Adder #(.width(1)) adder_4 (.a(adder_3_cout), .b(and_4_out), .out(adder_4_out), .cout(adder_4_cout));  // open: cin
  Adder #(.width(1)) adder_5 (.a(adder_4_cout), .b(and_3_out), .out(adder_5_out));  // open: cin, cout

  // Notes on the sheet:
  //   CP1
  //   CP2
endmodule
