// Logisim project DEC_INC_4bit.circ as structural Verilog: 1 circuit, main circuit main
module main (
  input  [3:0] A,
  input  C,
  input  A3,
  input  A2,
  input  A1,
  input  A0,
  input  C_2,
  output [3:0] OUT,
  output out_9,
  output out_10,
  output out_11,
  output out_12,
  output out_13,
  output out_14,
  output out_15,
  output out_16
);

  wire adder_3_cout, adder_4_cout, adder_5_cout, adder_6_out, adder_7_cout, adder_7_out, adder_8_cout,
       adder_8_out, adder_9_cout, adder_9_out, decoder_1_out0, decoder_1_out1, not_1_out, not_2_out,
       not_3_out, not_4_out;
  wire [3:0] adder_1_out, subtractor_1_out;

  not not_1 (not_1_out, A3);
  not not_2 (not_2_out, A2);
  not not_3 (not_3_out, A1);
  not not_4 (not_4_out, A0);
  Adder #(.width(4)) adder_1 (.a(A), .b(4'b0001), .out(adder_1_out));  // open: cin, cout
  Subtractor #(.width(4)) subtractor_1 (.a(A), .b(4'b0001), .out(subtractor_1_out));  // open: bin, bout
  Adder #(.width(1)) adder_2 (.a(A3), .b(adder_3_cout), .out(out_10));  // open: cin, cout
  Adder #(.width(1)) adder_3 (.a(A2), .b(adder_4_cout), .out(out_12), .cout(adder_3_cout));  // open: cin
  Adder #(.width(1)) adder_4 (.a(A1), .b(adder_5_cout), .out(out_14), .cout(adder_4_cout));  // open: cin
  Adder #(.width(1)) adder_5 (.a(A0), .b(decoder_1_out0), .out(out_16), .cout(adder_5_cout));  // open: cin
  Decoder decoder_1 (.out0(decoder_1_out0), .out1(decoder_1_out1), .sel(C_2), .en(1'b1));
  Multiplexer #(.width(4)) multiplexer_1 (.in0(adder_1_out), .in1(subtractor_1_out), .out(OUT), .sel(C));
  Adder #(.width(1)) adder_6 (.a(not_1_out), .b(adder_7_cout), .out(adder_6_out));  // open: cin, cout
  Adder #(.width(1)) adder_7 (.a(not_2_out), .b(adder_8_cout), .out(adder_7_out), .cout(adder_7_cout));  // open: cin
  Adder #(.width(1)) adder_8 (.a(not_3_out), .b(adder_9_cout), .out(adder_8_out), .cout(adder_8_cout));  // open: cin
  Adder #(.width(1)) adder_9 (.a(not_4_out), .b(decoder_1_out1), .out(adder_9_out), .cout(adder_9_cout));  // open: cin
  not not_5 (out_9, adder_6_out);
  not not_6 (out_11, adder_7_out);
  not not_7 (out_13, adder_8_out);
  not not_8 (out_15, adder_9_out);

  // Notes on the sheet:
  //   A + 1
  //   A - 1
  //   A + 1
  //   A - 1
endmodule
