// Logisim project esame_20_luglio_2016.circ as structural Verilog: 1 circuit, main circuit main
module main (
  input  A0,
  input  B0,
  input  A1,
  input  B1,
  input  A2,
  input  B2,
  input  A3,
  input  B3,
  output out_9
);

  wire and_1_out, and_2_out, not_1_out, xnor_1_out, xnor_2_out, xnor_3_out, xnor_4_out;

  and and_1 (and_1_out, A0, not_1_out);
  not not_1 (not_1_out, B0);
  xnor xnor_1 (xnor_1_out, A0, B0);
  xnor xnor_2 (xnor_2_out, A1, B1);
  xnor xnor_3 (xnor_3_out, A2, B2);
  xnor xnor_4 (xnor_4_out, A3, B3);
  and and_2 (and_2_out, xnor_1_out, xnor_2_out, xnor_3_out, xnor_4_out);
  or or_1 (out_9, and_1_out, and_2_out);
endmodule
