// Logisim project esercizio_2.circ as structural Verilog: 1 circuit, main circuit main
module main (
  input  in_1,
  input  in_2,
  input  in_3,
  input  in_4,
  input  S,
  input  in_6,
  input  in_7,
  input  in_8,
  input  in_9,
  output out_10
);

  wire d_ff_1_q, d_ff_2_q, d_ff_3_q, d_ff_4_q, d_ff_5_q, d_ff_6_q, d_ff_7_q, d_ff_8_q, not_1_out, not_2_out,
       not_3_out, not_4_out, xor_1_out, xor_2_out, xor_3_out, xor_4_out;

  D_Flip_Flop d_ff_1 (.D(in_1), .clk(S), .Q(d_ff_1_q));  // open: Qn, preset, reset
  D_Flip_Flop d_ff_2 (.D(in_2), .clk(S), .Q(d_ff_2_q));  // open: Qn, preset, reset
  D_Flip_Flop d_ff_3 (.D(in_3), .clk(S), .Q(d_ff_3_q));  // open: Qn, preset, reset
  D_Flip_Flop d_ff_4 (.D(in_4), .clk(S), .Q(d_ff_4_q));  // open: Qn, preset, reset
  D_Flip_Flop d_ff_5 (.D(in_6), .clk(S), .Q(d_ff_5_q));  // open: Qn, preset, reset
  D_Flip_Flop d_ff_6 (.D(in_7), .clk(S), .Q(d_ff_6_q));  // open: Qn, preset, reset
  D_Flip_Flop d_ff_7 (.D(in_8), .clk(S), .Q(d_ff_7_q));  // open: Qn, preset, reset
  D_Flip_Flop d_ff_8 (.D(in_9), .clk(S), .Q(d_ff_8_q));  // open: Qn, preset, reset
  xor xor_1 (xor_1_out, d_ff_1_q, d_ff_5_q);
  not not_1 (not_1_out, xor_1_out);
  xor xor_2 (xor_2_out, d_ff_2_q, d_ff_6_q);
  not not_2 (not_2_out, xor_2_out);
  xor xor_3 (xor_3_out, d_ff_3_q, d_ff_7_q);
  not not_3 (not_3_out, xor_3_out);
  xor xor_4 (xor_4_out, d_ff_4_q, d_ff_8_q);
  not not_4 (not_4_out, xor_4_out);
  and and_1 (out_10, not_1_out, not_2_out, not_3_out, not_4_out);
endmodule
