// Logisim project esercizio_5_esonero_2018.circ as structural Verilog: 1 circuit, main circuit main
module main (
  input  A1,
  input  A2,
  input  W,
  output B1,
  output B2,
  output B3
);

  wire xor_1_out;

  xor xor_1 (xor_1_out, A1, A2);
  D_Flip_Flop d_ff_1 (.D(A1), .clk(W), .Q(B1));  // open: Qn, preset, reset
  D_Flip_Flop d_ff_2 (.D(A2), .clk(W), .Q(B2));  // open: Qn, preset, reset
  D_Flip_Flop d_ff_3 (.D(xor_1_out), .clk(W), .Q(B3));  // open: Qn, preset, reset
endmodule
