// Logisim project modulo_4bit.circ as structural Verilog: 1 circuit, main circuit main
module main (
  input  A0,
  input  A1,
  input  A2,
  input  A3
);

  wire and_1_out, and_2_out, and_3_out, and_4_out, and_5_out, and_6_out, and_7_out, and_8_out,
       decoder_1_out0, decoder_1_out1, not_1_out, not_2_out, not_3_out, not_4_out, xnor_1_out;

  not not_1 (not_1_out, A0);
  not not_2 (not_2_out, A1);
  and and_1 (and_1_out, decoder_1_out1, not_1_out);
  and and_2 (and_2_out, A0, decoder_1_out0);
  not not_3 (not_3_out, A3);
  and and_3 (and_3_out, decoder_1_out1, not_2_out);
  and and_4 (and_4_out, A1, decoder_1_out0);
  not not_4 (not_4_out, A3);
  and and_5 (and_5_out, decoder_1_out1, not_3_out);
  and and_6 (and_6_out, A2, decoder_1_out0);
  xnor xnor_1 (xnor_1_out, A3, 1'b0);
  and and_7 (and_7_out, decoder_1_out1, not_4_out);
  and and_8 (and_8_out, A3, decoder_1_out0);
  Decoder decoder_1 (.out0(decoder_1_out0), .out1(decoder_1_out1), .sel(xnor_1_out), .en(1'b1));

  // Notes on the sheet:
  //   A0
  //   A0
  //   A1
  //   A1
  //   A2
  //   DA QUI POI FAI IL CP2 COME "ultimo_es_slide.circ"
  //   A2
  //   A3
  //   A3
  //   A>=0
  //   A<0
endmodule
