// Logisim project raddoppiatore.circ as structural Verilog: 1 circuit, main circuit main
module main (
  input  [3:0] in_1,
  input  in_2,
  output [3:0] out_3
);

  wire [3:0] shifter_1_out;

  Shifter #(.width(4)) shifter_1 (.in(in_1), .\dist (2'b01), .out(shifter_1_out));
  Multiplexer #(.width(4)) multiplexer_1 (.in0(in_1), .in1(shifter_1_out), .out(out_3), .sel(in_2));
endmodule
