// Logisim project registri_e_bit_di_parita.circ as structural Verilog: 1 circuit, main circuit main
module main (
  input  A1,
  input  A2,
  input  W,
  input  in_4,
  input  in_5,
  input  in_6,
  input  in_7,
  input  in_8,
  output B1,
  output B2,
  output B3
);

  wire undriven, xor_1_out, xor_2_out, xor_3_out, xor_4_out, xor_5_out;

  xor xor_1 (xor_1_out, in_4, in_5);
  xor xor_2 (xor_2_out, in_6, in_7);
  xor xor_3 (xor_3_out, A1, A2);
  xor xor_4 (xor_4_out, xor_1_out, xor_2_out);
  D_Flip_Flop d_ff_1 (.clk(W), .D(A1), .Q(B1));  // open: Qn, preset, reset
  D_Flip_Flop d_ff_2 (.clk(W), .D(A2), .Q(B2), .reset(undriven));  // open: Qn, preset
  D_Flip_Flop d_ff_3 (.clk(W), .D(xor_3_out), .Q(B3));  // open: Qn, preset, reset
  xor xor_5 (xor_5_out, in_8, xor_4_out);

  // Notes on the sheet:
  //   BIT DI PARITA'
  //   BIT DI PARITA' A 5 BIT
endmodule
