// Logisim project registro_contatore_4bit.circ as structural Verilog: 1 circuit, main circuit main
module main (
  input  A3,
  input  A2,
  input  A1,
  input  A0,
  input  C,
  input  [3:0] A,
  input  C_2,
  output out_8,
  output out_9,
  output out_10,
  output out_11,
  output out_12,
  output out_13,
  output out_14,
  output out_15,
  output [3:0] R,
  output [3:0] R___1
);

  wire and_1_out, and_2_out, and_3_out, and_4_out, and_6_out, and_7_out, and_8_out, decoder_1_out0,
       decoder_1_out1, decoder_2_out0;

  Decoder decoder_1 (.out0(decoder_1_out0), .out1(decoder_1_out1), .sel(C), .en(1'b1));
  Decoder decoder_2 (.out0(decoder_2_out0), .sel(C_2));  // open: out1, en
  D_Flip_Flop d_ff_1 (.clk(decoder_1_out0), .D(A3), .Q(out_8));  // open: Qn, preset, reset
  D_Flip_Flop d_ff_2 (.clk(decoder_1_out0), .D(A2), .Q(out_10));  // open: Qn, preset, reset
  D_Flip_Flop d_ff_3 (.clk(decoder_1_out0), .D(A1), .Q(out_12));  // open: Qn, preset, reset
  D_Flip_Flop d_ff_4 (.clk(decoder_1_out0), .D(A0), .Q(out_14));  // open: Qn, preset, reset
  Register #(.width(4)) register_1 (.D(A), .Q(R), .clk(decoder_2_out0));  // open: en, clr
  Adder #(.width(4)) adder_1 (.a(R), .b(4'b0001), .out(R___1));  // open: cin, cout
  and and_1 (and_1_out, decoder_1_out1, out_8);
  and and_2 (and_2_out, decoder_1_out1, out_10);
  and and_3 (and_3_out, decoder_1_out1, out_12);
  and and_4 (and_4_out, decoder_1_out1, out_14);
  xor xor_1 (out_9, and_1_out, and_6_out);
  xor xor_2 (out_11, and_2_out, and_7_out);
  xor xor_3 (out_13, and_3_out, and_8_out);
  xor xor_4 (out_15, and_4_out, decoder_1_out1);
  // AND_Gate and_5 has open pins: in0=and_6_out, in1=and_1_out, out=open
  and and_6 (and_6_out, and_7_out, and_1_out);
  and and_7 (and_7_out, and_2_out, and_8_out);
  and and_8 (and_8_out, and_4_out, decoder_1_out1);
endmodule
