// Logisim project scorritorecontrollato_2bit.circ as structural Verilog: 1 circuit, main circuit main
module main (
  input  [1:0] in_1,
  input  in_2,
  output [1:0] out_3
);

  wire [1:0] shifter_1_out, shifter_2_out;

  Shifter #(.width(2)) shifter_1 (.in(in_1), .\dist (1'b1), .out(shifter_1_out));
  Shifter #(.shift("lr"), .width(2)) shifter_2 (.in(in_1), .\dist (1'b1), .out(shifter_2_out));
  Multiplexer #(.width(2)) multiplexer_1 (.in0(shifter_1_out), .in1(shifter_2_out), .out(out_3), .sel(in_2));
endmodule
