// Logisim project secondo_esercizio_slide.circ as structural Verilog: 1 circuit, main circuit main
module main (
  input  A,
  input  B,
  input  C
);

  wire multiplexer_1_out, not_1_out, xnor_1_out;

  xnor xnor_1 (xnor_1_out, A, B);
  not not_1 (not_1_out, xnor_1_out);
  Multiplexer multiplexer_1 (.in0(xnor_1_out), .in1(not_1_out), .out(multiplexer_1_out), .sel(C));

  // Notes on the sheet:
  //   A = B
  //   A != B
  //   P
endmodule
