// Logisim project semplice_ALU.circ as structural Verilog: 1 circuit, main circuit main
module main (
  input  in_1,
  input  A,
  input  B,
  input  F0,
  input  F1,
  input  [1:0] in_6,
  input  [1:0] in_7,
  output out_8
);

  wire adder_1_out, and_1_out, and_2_out, and_3_out, and_4_out, and_5_out, D0_out, D1_out, D2_out, D3_out,
       decoder_1_out0, decoder_1_out1, decoder_1_out2, decoder_1_out3, multiplexer_1_out, not_1_out,
       not_2_out, not_3_out, or_1_out, undriven, undriven_2, undriven_3, undriven_4, undriven_5, xnor_1_out;

  not not_1 (not_1_out, F0);
  not not_2 (not_2_out, F1);
  and D0 (D0_out, not_2_out, not_1_out);
  Decoder #(.select(2)) decoder_1 (
    .out0(decoder_1_out0), .out1(decoder_1_out1), .out2(decoder_1_out2), .out3(decoder_1_out3), .sel(in_6),
    .en(undriven));
  and D1 (D1_out, not_1_out, F1);
  and D2 (D2_out, F0, not_2_out);
  not not_3 (not_3_out, A);
  xnor xnor_1 (xnor_1_out, A, B);
  Adder #(.width(1)) adder_1 (.a(A), .b(B), .out(adder_1_out), .cin(in_1), .cout(out_8));
  and and_1 (and_1_out, A, B);
  and D3 (D3_out, F0, F1);
  Multiplexer #(.select(2)) multiplexer_1 (
    .in0(undriven_2), .in1(undriven_3), .in2(undriven_4), .in3(undriven_5), .out(multiplexer_1_out),
    .sel(in_7));
  and and_2 (and_2_out, not_3_out, D0_out);
  and and_3 (and_3_out, xnor_1_out, D1_out);
  and and_4 (and_4_out, adder_1_out, D2_out);
  and and_5 (and_5_out, and_1_out, D3_out);
  or or_1 (or_1_out, and_2_out, and_3_out, and_4_out, and_5_out);

  // Notes on the sheet:
  //   O
endmodule
