// Logisim project semplice_ALU4bit.circ as structural Verilog: 1 circuit, main circuit main
module main (
  input  in_1,
  input  [3:0] A,
  input  [3:0] B,
  input  [1:0] C,
  input  in_5,
  input  A3,
  input  A2,
  input  A1,
  input  A0,
  input  B3,
  input  B2,
  input  B1,
  input  B0,
  input  in_14,
  input  [3:0] in_15,
  input  [1:0] C_2,
  input  [3:0] CP2,
  input  [3:0] in_18,
  input  in_19,
  input  in_20,
  input  in_21,
  input  [3:0] in_22,
  input  [1:0] in_23,
  input  A0_2,
  input  A1_2,
  input  in_26,
  input  in_27,
  input  A2_2,
  input  A3_2,
  output [3:0] OUT,
  output out_31,
  output out_32,
  output [3:0] out_33,
  output [3:0] out_34,
  output [3:0] out_35,
  output B0_2,
  output B1_2,
  output B2_2,
  output B3_2
);

  wire adder_2_out, adder_3_out, adder_4_cout, adder_4_out, adder_5_cout, adder_5_out, adder_6_out,
       adder_7_cout, adder_7_out, adder_8_cout, adder_8_out, adder_9_cout, adder_9_out, adder_11_cout,
       adder_12_cout, adder_13_cout, and_1_out, and_2_out, and_3_out, and_4_out, and_5_out, and_6_out,
       and_7_out, and_8_out, decoder_1_out0, decoder_1_out2, decoder_1_out3, not_2_out, not_3_out, not_4_out,
       not_5_out, not_6_out, not_7_out, not_9_out, not_10_out, not_11_out, not_12_out;
  wire [3:0] adder_1_out, not_1_out, not_8_out, subtractor_1_out;

  Decoder #(.select(2)) decoder_1 (
    .out0(decoder_1_out0), .out1(A0), .out2(decoder_1_out2), .out3(decoder_1_out3), .sel(C_2), .en(1'b1));
  assign not_1_out = ~B;  // NOT_Gate not_1, 4 bits wide
  Adder #(.width(4)) adder_1 (.a(A), .b(B), .out(adder_1_out), .cin(in_1), .cout(out_31));
  Subtractor #(.width(4)) subtractor_1 (.a(A), .b(B), .out(subtractor_1_out), .bin(in_5), .bout(out_32));
  and and_1 (and_1_out, A3, decoder_1_out0);
  and and_2 (and_2_out, A2, decoder_1_out0);
  and and_3 (and_3_out, A1, decoder_1_out0);
  and and_4 (and_4_out, A0, decoder_1_out0);
  not not_2 (not_2_out, B3);
  not not_3 (not_3_out, B2);
  not not_4 (not_4_out, B1);
  not not_5 (not_5_out, B0);
  and and_5 (and_5_out, not_2_out, A0);
  and and_6 (and_6_out, not_3_out, A0);
  and and_7 (and_7_out, not_4_out, A0);
  and and_8 (and_8_out, not_5_out, A0);
  not not_6 (not_6_out, in_20);
  Adder #(.width(1)) adder_2 (.a(not_6_out), .b(1'b0), .out(adder_2_out), .cin(adder_4_cout));  // open: cout
  Adder #(.width(1)) adder_3 (.a(adder_2_out), .b(in_26), .out(adder_3_out), .cin(adder_5_cout));  // open: cout
  not not_7 (not_7_out, in_21);
  Adder #(.width(1)) adder_4 (.a(not_7_out), .b(1'b0), .out(adder_4_out), .cin(1'b1), .cout(adder_4_cout));
  Adder #(.width(1)) adder_5 (.a(adder_4_out), .b(in_27), .out(adder_5_out), .cout(adder_5_cout));  // open: cin
  Adder #(.width(1)) adder_6 (.a(A3), .b(B3), .out(adder_6_out), .cin(adder_7_cout));  // open: cout
  Adder #(.width(1)) adder_7 (.a(A2), .b(B2), .out(adder_7_out), .cin(adder_8_cout), .cout(adder_7_cout));
  Adder #(.width(1)) adder_8 (.a(A1), .b(B1), .out(adder_8_out), .cin(adder_9_cout), .cout(adder_8_cout));
  Adder #(.width(1)) adder_9 (.a(A0), .b(B0), .out(adder_9_out), .cout(adder_9_cout));  // open: cin
  Multiplexer #(.select(2), .width(4)) multiplexer_1 (
    .in0(A), .in1(not_1_out), .in2(adder_1_out), .in3(subtractor_1_out), .out(OUT), .sel(C));
  // OR_Gate or_1 has open pins: in0=and_1_out, in1=adder_6_out, in2=and_5_out, out=open
  // OR_Gate or_2 has open pins: in0=and_2_out, in1=adder_7_out, in2=and_6_out, out=open
  // OR_Gate or_3 has open pins: in0=and_3_out, in1=adder_8_out, in2=and_7_out, out=open
  // OR_Gate or_4 has open pins: in0=and_4_out, in1=adder_9_out, in2=and_8_out, out=open
  assign not_8_out = ~CP2;  // NOT_Gate not_8, 4 bits wide
  Shifter #(.shift("lr"), .width(4)) shifter_1 (.in(in_22), .\dist (in_23), .out(out_35));
  Adder #(.width(4)) adder_10 (.a(not_8_out), .b(4'b0001), .out(out_33));  // open: cin, cout
  not not_9 (not_9_out, A0_2);
  not not_10 (not_10_out, A1_2);
  not not_11 (not_11_out, A2_2);
  not not_12 (not_12_out, A3_2);
  Adder #(.width(1)) adder_11 (.a(1'b1), .b(not_9_out), .out(B0_2), .cout(adder_11_cout));  // open: cin
  Adder #(.width(1)) adder_12 (.a(adder_11_cout), .b(not_10_out), .out(B1_2), .cout(adder_12_cout));  // open: cin
  Adder #(.width(1)) adder_13 (.a(adder_12_cout), .b(not_11_out), .out(B2_2), .cout(adder_13_cout));  // open: cin
  Adder #(.width(1)) adder_14 (.a(adder_13_cout), .b(not_12_out), .out(B3_2));  // open: cin, cout
  Subtractor #(.width(4)) subtractor_2 (.a(in_15), .b(in_18), .out(out_34), .bin(in_14), .bout(in_19));

  // Notes on the sheet:
  //   A + B
  //   !B
  //   A - B
  //   A
  //   sottrattore
  //   SHIFTER A DESTRA
  //   SOTTRATTORE CON RIPORTI
  //   CP2
endmodule
