// Logisim project sottrattore_4bit_con_CP2.circ as structural Verilog: 1 circuit, main circuit main
module main (
  input  [3:0] X,
  input  [3:0] Y,
  output [3:0] SOTT
);

  wire [3:0] adder_1_out, not_1_out;

  assign not_1_out = ~Y;  // NOT_Gate not_1, 4 bits wide
  Adder #(.width(4)) adder_1 (.a(not_1_out), .b(4'b0001), .out(adder_1_out));  // open: cin, cout
  Adder #(.width(4)) adder_2 (.a(X), .b(adder_1_out), .out(SOTT), .cin(1'b0));  // open: cout

  // Notes on the sheet:
  //   Y IN CP2
endmodule
