// Logisim project ultimo_es_slide.circ as structural Verilog: 1 circuit, main circuit main
module main (
  input  X0,
  input  X1,
  input  X2,
  input  X3,
  input  C,
  input  S,
  output Y0,
  output Y1,
  output Y2,
  output Y3,
  output out_11,
  output out_12,
  output CP2,
  output out_14
);

  wire and_1_out, and_2_out, and_3_out, and_4_out, and_5_out, and_6_out, and_7_out, and_8_out, and_9_out,
       and_10_out, not_1_out, not_2_out, not_3_out, not_4_out, xnor_1_out, xnor_2_out, xnor_3_out, xnor_4_out;

  and and_1 (and_1_out, xnor_1_out, xnor_2_out);
  xnor xnor_1 (xnor_1_out, 1'b1, C);
  D_Flip_Flop d_ff_1 (.clk(and_1_out), .D(X0), .Q(Y0));  // open: Qn, preset, reset
  D_Flip_Flop d_ff_2 (.clk(and_1_out), .D(X1), .Q(Y1));  // open: Qn, preset, reset
  D_Flip_Flop d_ff_3 (.clk(and_1_out), .D(X2), .Q(Y2));  // open: Qn, preset, reset
  D_Flip_Flop d_ff_4 (.clk(and_1_out), .D(X3), .Q(Y3));  // open: Qn, preset, reset
  xnor xnor_2 (xnor_2_out, S, 1'b0);
  and and_2 (and_2_out, xnor_3_out, xnor_4_out);
  xnor xnor_3 (xnor_3_out, 1'b1, S);
  xnor xnor_4 (xnor_4_out, C, 1'b0);
  not not_1 (not_1_out, Y0);
  not not_2 (not_2_out, Y1);
  not not_3 (not_3_out, Y2);
  not not_4 (not_4_out, Y3);
  and and_3 (and_3_out, not_1_out, and_2_out);
  and and_4 (and_4_out, not_2_out, and_2_out);
  and and_5 (and_5_out, not_3_out, and_2_out);
  and and_6 (and_6_out, not_4_out, and_2_out);
  and and_7 (and_7_out, and_6_out, 1'b1);
  and and_8 (and_8_out, and_5_out, and_7_out);
  and and_9 (and_9_out, and_4_out, and_7_out);
  and and_10 (and_10_out, and_3_out, and_7_out);
  xor xor_1 (out_14, and_6_out, 1'b1);
  xor xor_2 (CP2, and_8_out, and_5_out);
  xor xor_3 (out_12, and_9_out, and_4_out);
  xor xor_4 (out_11, and_10_out, and_3_out);

  // Notes on the sheet:
  //   S = 0 e C = 1
  //   S = 1 e C = 0
  //   CP1
endmodule
