// Logisim project es1hw3.circ as structural Verilog: 1 circuit, main circuit main
module main (
  input  A,
  input  B,
  input  C,
  output _2_zeri,
  output out_5
);

  wire and_1_out, nand_1_out, not_1_out, not_2_out, not_3_out, not_4_out, xor_1_out;

  not not_1 (not_1_out, C);
  not not_2 (not_2_out, B);
  not not_3 (not_3_out, A);
  and and_1 (and_1_out, not_1_out, not_2_out, not_3_out);
  ExactlyOne xor_1 (.out(xor_1_out), .in0(A), .in1(B), .in2(C));
  nand nand_1 (nand_1_out, A, C, B);
  not not_4 (not_4_out, xor_1_out);
  and and_2 (out_5, not_4_out, nand_1_out);
  or or_1 (_2_zeri, xor_1_out, and_1_out);

  // Notes on the sheet:
  //   1 zero
endmodule
