// Logisim project esercizio2.circ as structural Verilog: 1 circuit, main circuit main
module main (
  input  A,
  input  B,
  input  C,
  input  D,
  input  clock,
  input  clear,
  input  [1:0] WS,
  output out_8,
  output out_9,
  output out_10,
  output out_11
);

  wire and_1_out, and_2_out, and_3_out, and_4_out, and_5_out, and_6_out, and_7_out, and_8_out, and_9_out,
       and_10_out, and_11_out, and_12_out, decoder_1_out0, decoder_1_out1, decoder_1_out2, decoder_1_out3,
       or_1_out, or_2_out, or_3_out, or_4_out;

  Decoder #(.enable("false"), .select(2)) decoder_1 (
    .out0(decoder_1_out0), .out1(decoder_1_out1), .out2(decoder_1_out2), .out3(decoder_1_out3), .sel(WS));
  LED led_1 (.in(decoder_1_out3));
  and and_1 (and_1_out, out_11, decoder_1_out1);
  and and_2 (and_2_out, out_8, decoder_1_out1);
  and and_3 (and_3_out, out_9, decoder_1_out1);
  and and_4 (and_4_out, out_10, decoder_1_out1);
  and and_5 (and_5_out, out_8, decoder_1_out0);
  and and_6 (and_6_out, out_9, decoder_1_out0);
  and and_7 (and_7_out, out_10, decoder_1_out0);
  and and_8 (and_8_out, out_11, decoder_1_out0);
  and and_9 (and_9_out, A, decoder_1_out2);
  and and_10 (and_10_out, B, decoder_1_out2);
  and and_11 (and_11_out, C, decoder_1_out2);
  and and_12 (and_12_out, D, decoder_1_out2);
  or or_1 (or_1_out, and_9_out, and_5_out, and_1_out);
  or or_2 (or_2_out, and_10_out, and_6_out, and_2_out);
  or or_3 (or_3_out, and_11_out, and_7_out, and_3_out);
  or or_4 (or_4_out, and_12_out, and_8_out, and_4_out);
  D_Flip_Flop d_ff_1 (.D(or_1_out), .clk(clock), .Q(out_8), .reset(clear));  // open: Qn, preset
  D_Flip_Flop d_ff_2 (.D(or_2_out), .clk(clock), .Q(out_9), .reset(clear));  // open: Qn, preset
  D_Flip_Flop d_ff_3 (.D(or_3_out), .clk(clock), .Q(out_10), .reset(clear));  // open: Qn, preset
  D_Flip_Flop d_ff_4 (.D(or_4_out), .clk(clock), .Q(out_11), .reset(clear));  // open: Qn, preset

  // Notes on the sheet:
  //   Errore
endmodule
