// Logisim project somma1.circ as structural Verilog: 1 circuit, main circuit main
module main (
  input  C,
  input  A,
  input  B,
  output out_4,
  output out_5
);

  wire adder_1_cout, adder_1_out, adder_2_out, and_1_out, and_2_out, and_3_out, and_4_out, clock_1_out,
       not_1_out, or_1_out, or_2_out;

  not not_1 (not_1_out, C);
  and and_1 (and_1_out, not_1_out, A);
  and and_2 (and_2_out, not_1_out, B);
  Adder #(.width(1)) adder_1 (.a(out_4), .b(C), .out(adder_1_out), .cout(adder_1_cout));  // open: cin
  Adder #(.width(1)) adder_2 (.a(adder_1_cout), .b(out_5), .out(adder_2_out));  // open: cin, cout
  and and_3 (and_3_out, adder_1_out, C);
  and and_4 (and_4_out, adder_2_out, C);
  Clock clock_1 (.out(clock_1_out));
  or or_1 (or_1_out, and_3_out, and_1_out);
  or or_2 (or_2_out, and_4_out, and_2_out);
  D_Flip_Flop d_ff_1 (.clk(clock_1_out), .D(or_1_out), .Q(out_4));  // open: Qn, preset, en, reset
  D_Flip_Flop d_ff_2 (.clk(clock_1_out), .D(or_2_out), .Q(out_5));  // open: Qn, preset, en, reset
endmodule
