// Logisim project c1_c2.circ as structural Verilog: 1 circuit, main circuit main
module main (
  input  in_1,
  input  in_2,
  input  in_3,
  input  in_4,
  input  in_5,
  output out_6,
  output out_7,
  output out_8,
  output out_9
);

  wire adder_1_cout, adder_1_out, adder_2_cout, adder_2_out, adder_3_cout, adder_3_out, adder_4_out,
       and_1_out, and_2_out, and_3_out, and_4_out, and_5_out, and_6_out, and_7_out, and_8_out, not_1_out,
       not_2_out, not_3_out, not_4_out, not_5_out, not_6_out, not_7_out, not_8_out, not_9_out;

  not not_1 (not_1_out, in_1);
  not not_2 (not_2_out, in_2);
  not not_3 (not_3_out, in_3);
  not not_4 (not_4_out, in_4);
  not not_5 (not_5_out, in_5);
  and and_1 (and_1_out, not_5_out, not_1_out);
  and and_2 (and_2_out, not_5_out, not_2_out);
  and and_3 (and_3_out, not_5_out, not_3_out);
  and and_4 (and_4_out, not_5_out, not_4_out);
  not not_6 (not_6_out, in_1);
  not not_7 (not_7_out, in_2);
  not not_8 (not_8_out, in_3);
  not not_9 (not_9_out, in_4);
  Adder #(.width(1)) adder_1 (.a(not_6_out), .b(1'b0), .out(adder_1_out), .cin(1'b1), .cout(adder_1_cout));
  Adder #(.width(1)) adder_2 (.a(not_7_out), .b(1'b0), .out(adder_2_out), .cin(adder_1_cout), .cout(adder_2_cout));
  Adder #(.width(1)) adder_3 (.a(not_8_out), .b(1'b0), .out(adder_3_out), .cin(adder_2_cout), .cout(adder_3_cout));
  Adder #(.width(1)) adder_4 (.a(not_9_out), .b(1'b0), .out(adder_4_out), .cin(adder_3_cout));  // open: cout
  and and_5 (and_5_out, in_5, adder_1_out);
  and and_6 (and_6_out, in_5, adder_2_out);
  and and_7 (and_7_out, in_5, adder_3_out);
  and and_8 (and_8_out, in_5, adder_4_out);
  or or_1 (out_6, and_1_out, and_5_out);
  or or_2 (out_7, and_2_out, and_6_out);
  or or_3 (out_8, and_3_out, and_7_out);
  or or_4 (out_9, and_8_out, and_4_out);
endmodule
