// Logisim project registrioIncrementato.circ as structural Verilog: 1 circuit, main circuit main
module main (
  input  in_1,
  input  in_2,
  input  in_3,
  input  in_4,
  input  in_5,
  output out_6,
  output out_7,
  output out_8,
  output out_9
);

  wire adder_1_cout, adder_1_out, adder_2_cout, adder_2_out, adder_3_cout, adder_3_out, adder_4_cout,
       adder_4_out, and_1_out, and_2_out, and_3_out, and_4_out, and_5_out, and_6_out, and_7_out, and_8_out,
       d_ff_1_q, d_ff_2_q, d_ff_3_q, d_ff_4_q, not_1_out;

  D_Flip_Flop d_ff_1 (.clk(not_1_out), .D(in_1), .Q(d_ff_1_q));  // open: Qn, preset, en, reset
  D_Flip_Flop d_ff_2 (.clk(not_1_out), .D(in_2), .Q(d_ff_2_q));  // open: Qn, preset, en, reset
  D_Flip_Flop d_ff_3 (.clk(not_1_out), .D(in_3), .Q(d_ff_3_q));  // open: Qn, preset, en, reset
  D_Flip_Flop d_ff_4 (.clk(not_1_out), .D(in_4), .Q(d_ff_4_q));  // open: Qn, preset, en, reset
  not not_1 (not_1_out, in_5);
  Adder #(.width(1)) adder_1 (.a(d_ff_1_q), .b(1'b0), .out(adder_1_out), .cin(1'b1), .cout(adder_1_cout));
  Adder #(.width(1)) adder_2 (.a(d_ff_2_q), .b(1'b0), .out(adder_2_out), .cin(adder_1_cout), .cout(adder_2_cout));
  Adder #(.width(1)) adder_3 (.a(d_ff_3_q), .b(1'b0), .out(adder_3_out), .cin(adder_2_cout), .cout(adder_3_cout));
  Adder #(.width(1)) adder_4 (.a(d_ff_4_q), .b(1'b0), .out(adder_4_out), .cin(adder_3_cout), .cout(adder_4_cout));
  and and_1 (and_1_out, d_ff_1_q, not_1_out);
  and and_2 (and_2_out, d_ff_2_q, not_1_out);
  and and_3 (and_3_out, d_ff_3_q, not_1_out);
  and and_4 (and_4_out, d_ff_4_q, not_1_out);
  and and_5 (and_5_out, in_5, adder_1_out);
  and and_6 (and_6_out, in_5, adder_2_out);
  and and_7 (and_7_out, in_5, adder_3_out);
  and and_8 (and_8_out, in_5, adder_4_out);
  or or_1 (out_6, and_1_out, and_5_out);
  or or_2 (out_7, and_2_out, and_6_out);
  or or_3 (out_8, and_3_out, and_7_out);
  or or_4 (out_9, and_4_out, and_8_out);
endmodule
