// Logisim project salvo_C2.circ as structural Verilog: 1 circuit, main circuit main
module main (
  input  in_1,
  input  in_2,
  input  in_3,
  input  in_4,
  output out_5,
  output out_6,
  output out_7,
  output out_8,
  output out_9,
  output out_10
);

  wire adder_1_cout, adder_2_cout, not_1_out, not_2_out, not_3_out;

  D_Flip_Flop d_ff_1 (.clk(in_4), .D(in_1), .Q(out_5));  // open: Qn, preset, en, reset
  D_Flip_Flop d_ff_2 (.clk(in_4), .D(in_2), .Q(out_6));  // open: Qn, preset, en, reset
  D_Flip_Flop d_ff_3 (.clk(in_4), .D(in_3), .Q(out_7));  // open: Qn, preset, en, reset
  not not_1 (not_1_out, out_5);
  not not_2 (not_2_out, out_6);
  not not_3 (not_3_out, out_7);
  Adder #(.width(1)) adder_1 (.a(not_1_out), .b(1'b0), .out(out_8), .cin(1'b1), .cout(adder_1_cout));
  Adder #(.width(1)) adder_2 (.a(not_2_out), .b(1'b0), .out(out_9), .cin(adder_1_cout), .cout(adder_2_cout));
  Adder #(.width(1)) adder_3 (.a(not_3_out), .b(1'b0), .out(out_10), .cin(adder_2_cout));  // open: cout
endmodule
