// Logisim project Esercizio1_VeronicaCatalano.circ as structural Verilog: 1 circuit, main circuit main
module main (
  input  A,
  input  B,
  input  C,
  output out_4,
  output out_5
);

  wire and_1_out, and_2_out, and_3_out, and_4_out, and_5_out, not_1_out, not_2_out, not_3_out, not_4_out,
       not_5_out, xor_1_out, xor_2_out, xor_3_out;

  not not_1 (not_1_out, A);
  not not_2 (not_2_out, B);
  not not_3 (not_3_out, C);
  not not_4 (not_4_out, A);
  xor xor_1 (xor_1_out, A, B);
  xor xor_2 (xor_2_out, not_3_out, C);
  and and_1 (and_1_out, not_1_out, not_2_out);
  xor xor_3 (xor_3_out, B, C);
  not not_5 (not_5_out, xor_3_out);
  and and_2 (and_2_out, xor_1_out, not_3_out);
  and and_3 (and_3_out, xor_2_out, and_1_out);
  and and_4 (and_4_out, not_5_out, not_5_out, not_4_out);
  and and_5 (and_5_out, A, xor_3_out);
  or or_1 (out_4, and_2_out, and_3_out);
  or or_2 (out_5, and_4_out, and_5_out);
endmodule
