// Logisim project Esercizio2_VeronicaCatalano.circ as structural Verilog: 1 circuit, main circuit main
module main (
  input  A1,
  input  A2,
  input  A3,
  input  A4,
  input  w,
  input  S,
  output B1,
  output B2,
  output B3,
  output B4
);

  wire and_1_out, and_2_out, and_3_out, and_4_out, and_5_out, not_1_out, not_2_out, not_3_out, s1_out,
       s2_out, s3_out, s4_out, sh_out, wr_out, xor_1_out, xor_2_out, xor_3_out, xor_4_out;

  not not_1 (not_1_out, w);
  not not_2 (not_2_out, S);
  and and_1 (and_1_out, A1, A1, wr_out);
  buf and_2 (and_2_out, A2);  // AND_Gate
  and and_3 (and_3_out, A3, A3);
  buf and_4 (and_4_out, A4);  // AND_Gate
  and wr (wr_out, w, w, not_2_out);
  and sh (sh_out, S, S, not_1_out);
  and and_5 (and_5_out, not_1_out, not_2_out);
  and s1 (s1_out, B4, sh_out);
  not not_3 (not_3_out, and_5_out);
  and s2 (s2_out, B1, sh_out, sh_out);
  and s3 (s3_out, B2, sh_out);
  and s4 (s4_out, B3, sh_out);
  xor xor_1 (xor_1_out, and_1_out, s1_out);
  xor xor_2 (xor_2_out, s2_out, and_2_out);
  xor xor_3 (xor_3_out, s3_out, and_3_out);
  xor xor_4 (xor_4_out, s4_out, and_4_out);
  D_Flip_Flop d_ff_1 (.D(xor_1_out), .Q(B1), .preset(not_3_out));  // open: clk, Qn, en, reset
  D_Flip_Flop d_ff_2 (.D(xor_2_out), .Q(B2), .preset(not_3_out));  // open: clk, Qn, en, reset
  D_Flip_Flop d_ff_3 (.D(xor_3_out), .Q(B3), .en(not_3_out));  // open: clk, Qn, preset, reset
  D_Flip_Flop d_ff_4 (.D(xor_4_out), .Q(B4), .preset(not_3_out), .en(not_3_out));  // open: clk, Qn, reset
endmodule
