// Logisim project alu.circ as structural Verilog: 1 circuit, main circuit main
module main (
  input  in_1,
  input  A,
  input  B,
  input  [1:0] in_4,
  output out_5,
  output out_6
);

  wire adder_1_cout, adder_1_out, and_1_out, and_3_out, and_4_out, and_5_out, and_6_out, decoder_1_out0,
       decoder_1_out1, decoder_1_out2, decoder_1_out3, not_1_out, xnor_1_out;

  Decoder #(.select(2)) decoder_1 (
    .out0(decoder_1_out0), .out1(decoder_1_out1), .out2(decoder_1_out2), .out3(decoder_1_out3), .sel(in_4),
    .en(1'b1));
  not not_1 (not_1_out, A);
  and and_1 (and_1_out, A, B);
  xnor xnor_1 (xnor_1_out, A, B);
  and and_2 (out_6, decoder_1_out1, adder_1_cout);
  Adder #(.width(1)) adder_1 (.a(A), .b(B), .out(adder_1_out), .cin(in_1), .cout(adder_1_cout));
  and and_3 (and_3_out, decoder_1_out0, decoder_1_out0, not_1_out);
  and and_4 (and_4_out, decoder_1_out2, and_1_out);
  and and_5 (and_5_out, decoder_1_out3, xnor_1_out);
  and and_6 (and_6_out, decoder_1_out1, adder_1_out);
  or or_1 (out_5, and_3_out, and_6_out, and_4_out, and_5_out);
endmodule
