// Logisim project comparatore_registri.circ as structural Verilog: 1 circuit, main circuit main
module main (
  input  in_1,
  input  in_2,
  input  in_3,
  input  in_4,
  input  in_5,
  input  in_6,
  input  in_7,
  input  in_8,
  input  w,
  output out_10
);

  wire d_ff_1_q, d_ff_2_q, d_ff_3_q, d_ff_4_q, d_ff_5_q, d_ff_6_q, d_ff_7_q, d_ff_8_q, xor_1_out, xor_2_out,
       xor_3_out, xor_4_out;

  D_Flip_Flop d_ff_1 (.clk(in_7), .D(in_1), .Q(d_ff_1_q));  // open: Qn, preset, en, reset
  D_Flip_Flop d_ff_2 (.clk(in_7), .D(in_2), .Q(d_ff_2_q));  // open: Qn, preset, en, reset
  D_Flip_Flop d_ff_3 (.clk(in_7), .D(in_3), .Q(d_ff_3_q));  // open: Qn, preset, en, reset
  D_Flip_Flop d_ff_4 (.clk(in_7), .D(in_4), .Q(d_ff_4_q));  // open: Qn, preset, en, reset
  D_Flip_Flop d_ff_5 (.clk(in_7), .D(in_5), .Q(d_ff_5_q));  // open: Qn, preset, en, reset
  D_Flip_Flop d_ff_6 (.clk(in_7), .D(in_6), .Q(d_ff_6_q));  // open: Qn, preset, en, reset
  D_Flip_Flop d_ff_7 (.clk(in_7), .D(in_7), .Q(d_ff_7_q));  // open: Qn, preset, en, reset
  D_Flip_Flop d_ff_8 (.clk(in_7), .D(in_8), .Q(d_ff_8_q));  // open: Qn, preset, en, reset
  xor xor_1 (xor_1_out, d_ff_1_q, d_ff_5_q);
  xor xor_2 (xor_2_out, d_ff_2_q, d_ff_6_q);
  xor xor_3 (xor_3_out, d_ff_3_q, d_ff_7_q);
  xor xor_4 (xor_4_out, d_ff_4_q, d_ff_8_q);
  nor nor_1 (out_10, xor_1_out, xor_2_out, xor_3_out, xor_4_out);

  assign w = in_7;
endmodule
