// Logisim project parita.circ as structural Verilog: 1 circuit, main circuit main
module main (
  input  in_1,
  input  in_2,
  input  in_3,
  output out_4,
  output out_5,
  output out_6
);

  wire xor_1_out;

  xor xor_1 (xor_1_out, in_1, in_2);
  D_Flip_Flop d_ff_1 (.clk(in_3), .D(in_1), .Q(out_4));  // open: Qn, preset, en, reset
  D_Flip_Flop d_ff_2 (.clk(in_3), .D(in_2), .Q(out_5));  // open: Qn, preset, en, reset
  D_Flip_Flop d_ff_3 (.clk(in_3), .D(xor_1_out), .Q(out_6));  // open: Qn, preset, en, reset
endmodule
