// Logisim project somma_diff.circ as structural Verilog: 1 circuit, main circuit main
module main (
  input  in_1,
  input  in_2,
  input  in_3,
  input  in_4,
  input  in_5,
  output out_6,
  output out_7,
  output out_8,
  output out_9
);

  wire adder_1_out, adder_2_cout, adder_2_out, adder_3_cout, adder_3_out, adder_4_cout, adder_4_out,
       adder_5_out, adder_6_cout, adder_6_out, adder_7_cout, adder_7_out, adder_8_cout, adder_8_out,
       and_1_out, and_2_out, and_3_out, and_4_out, and_5_out, and_6_out, and_7_out, and_8_out, not_1_out,
       not_2_out, not_3_out, not_4_out, not_5_out, not_6_out, not_7_out, not_8_out, not_9_out;

  not not_1 (not_1_out, in_5);
  Adder #(.width(1)) adder_1 (.a(in_1), .b(adder_2_cout), .out(adder_1_out));  // open: cin, cout
  Adder #(.width(1)) adder_2 (.a(in_2), .b(adder_3_cout), .out(adder_2_out), .cout(adder_2_cout));  // open: cin
  Adder #(.width(1)) adder_3 (.a(in_3), .b(adder_4_cout), .out(adder_3_out), .cout(adder_3_cout));  // open: cin
  Adder #(.width(1)) adder_4 (.a(in_4), .b(not_1_out), .out(adder_4_out), .cout(adder_4_cout));  // open: cin
  not not_2 (not_2_out, in_1);
  not not_3 (not_3_out, in_2);
  not not_4 (not_4_out, in_3);
  not not_5 (not_5_out, in_4);
  and and_1 (and_1_out, adder_1_out, not_1_out);
  and and_2 (and_2_out, adder_2_out, not_1_out);
  and and_3 (and_3_out, adder_3_out, not_1_out);
  and and_4 (and_4_out, adder_4_out, not_1_out);
  Adder #(.width(1)) adder_5 (.a(not_2_out), .b(adder_6_cout), .out(adder_5_out));  // open: cin, cout
  Adder #(.width(1)) adder_6 (.a(not_3_out), .b(adder_7_cout), .out(adder_6_out), .cout(adder_6_cout));  // open: cin
  Adder #(.width(1)) adder_7 (.a(not_4_out), .b(adder_8_cout), .out(adder_7_out), .cout(adder_7_cout));  // open: cin
  Adder #(.width(1)) adder_8 (.a(not_5_out), .b(in_5), .out(adder_8_out), .cout(adder_8_cout));  // open: cin
  not not_6 (not_6_out, adder_5_out);
  not not_7 (not_7_out, adder_6_out);
  not not_8 (not_8_out, adder_7_out);
  not not_9 (not_9_out, adder_8_out);
  and and_5 (and_5_out, in_5, not_6_out);
  and and_6 (and_6_out, not_7_out, in_5);
  and and_7 (and_7_out, not_8_out, in_5);
  and and_8 (and_8_out, not_9_out, in_5);
  or or_1 (out_6, and_1_out, and_5_out);
  or or_2 (out_7, and_2_out, and_6_out);
  or or_3 (out_8, and_3_out, and_7_out);
  or or_4 (out_9, and_4_out, and_8_out);
endmodule
