// Logisim project uguale_diversi.circ as structural Verilog: 1 circuit, main circuit main
module main (
  input  in_1,
  input  in_2,
  input  in_3,
  input  in_4,
  input  in_5,
  input  in_6,
  input  a1,
  input  a2,
  input  a3,
  input  w,
  output out_11,
  output out_12,
  output out_13,
  output out_14,
  output b1,
  output b2,
  output b3,
  output c1,
  output c2,
  output c3
);

  wire adder_1_cout, adder_2_cout, and_1_out, and_2_out, nor_1_out, not_1_out, not_2_out, not_3_out,
       not_4_out, xor_1_out, xor_2_out;

  D_Flip_Flop d_ff_1 (.clk(w), .D(a1), .Q(b1));  // open: Qn, preset, en, reset
  D_Flip_Flop d_ff_2 (.clk(w), .D(a2), .Q(b2));  // open: Qn, preset, en, reset
  D_Flip_Flop d_ff_3 (.clk(w), .D(a3), .Q(b3));  // open: Qn, preset, en, reset
  D_Flip_Flop d_ff_4 (.clk(in_5), .D(in_1), .Q(out_11));  // open: Qn, preset, en, reset
  D_Flip_Flop d_ff_5 (.clk(in_5), .D(in_4), .Q(out_12));  // open: Qn, preset, en, reset
  xor xor_1 (xor_1_out, in_1, in_4);
  D_Flip_Flop d_ff_6 (.clk(in_5), .D(xor_1_out), .Q(out_14));  // open: Qn, preset, en, reset
  not not_1 (not_1_out, b1);
  not not_2 (not_2_out, b2);
  not not_3 (not_3_out, b3);
  Adder #(.width(1)) adder_1 (.a(not_1_out), .b(1'b0), .out(c1), .cin(1'b1), .cout(adder_1_cout));
  Adder #(.width(1)) adder_2 (.a(not_2_out), .b(1'b0), .out(c2), .cin(adder_1_cout), .cout(adder_2_cout));
  Adder #(.width(1)) adder_3 (.a(not_3_out), .b(1'b0), .out(c3), .cin(adder_2_cout));  // open: cout
  not not_4 (not_4_out, in_6);
  xor xor_2 (xor_2_out, in_2, in_3);
  and and_1 (and_1_out, xor_2_out, in_6);
  nor nor_1 (nor_1_out, in_2, in_3);
  and and_2 (and_2_out, nor_1_out, not_4_out);
  or or_1 (out_13, and_1_out, and_2_out);
endmodule
