// Logisim project Esercizio1TerzoHomework.circ as structural Verilog: 1 circuit, main circuit main
module main (
  input  in_1,
  input  in_2,
  input  in_3,
  output S0,
  output S1
);

  wire and_1_out, and_2_out, and_3_out, not_1_out, not_2_out, not_3_out;

  not not_1 (not_1_out, in_1);
  not not_2 (not_2_out, in_2);
  not not_3 (not_3_out, in_3);
  and and_1 (and_1_out, not_1_out, not_2_out);
  and and_2 (and_2_out, not_1_out, not_3_out);
  and and_3 (and_3_out, not_2_out, not_3_out);
  xor xor_1 (S0, not_1_out, not_2_out, not_3_out);
  or or_1 (S1, and_1_out, and_2_out, and_3_out);
endmodule
