// Logisim project Prova.circ as structural Verilog: 1 circuit, main circuit main
module main (
  input  in_1,
  input  in_2,
  input  in_3,
  input  in_4,
  input  in_5,
  input  in_6,
  output out_7,
  output out_8,
  output out_9,
  output out_10
);

  wire D0_q, D1_q, D2_q, D3_q;

  D_Flip_Flop D1 (.D(D2_q), .Q(D1_q));  // open: clk, Qn, preset, reset
  D_Flip_Flop D0 (.D(D1_q), .Q(D0_q));  // open: clk, Qn, preset, reset
  D_Flip_Flop D3 (.D(D0_q), .Q(D3_q));  // open: clk, Qn, preset, reset
  D_Flip_Flop D2 (.D(D3_q), .Q(D2_q));  // open: clk, Qn, preset, reset
  Clock clock_1 ();  // open: out
endmodule
